# Fritzing sketch Schaltplan (saved by Fritzing 0.9.3b)
breadboards: 1

parts:
  U1 = attiny85 [package=dip]  # not connected
  U2 = RF-LINK_RX [package=rf-link_rx]
  Q1 = PNP-Transistor [package="TO92 [THT]"]
  R1 = Resistor [tolerance=±5% resistance=220 package="2010 [SMD]"]

nets:
  N1: U2.GND, Q1.E
  N2: Q1.B, R1.Pin_0

notes:
  GND 5V+ DC IN1 IN2
  2 Fach Relais Module
  +5V DC GND (-)
  Spannungsversorgung
